// Logisim project Pacemaker.circ as structural Verilog: 7 circuits, main circuit main
module main (
  input  in_1,
  input  in_2,
  output out_3,
  output out_4
);

  wire clock_1_out, controller_1_ta, controller_1_tv, timera_1_za, timerv_1_zv;

  Clock clock_1 (.out(clock_1_out));
  Controller controller_1 (
    .pa(out_3), .ta(controller_1_ta), .pv(out_4), .tv(controller_1_tv), .sa(in_1), .za(timera_1_za),
    .sv(in_2), .zv(timerv_1_zv), .Clock(clock_1_out));
  TimerV timerv_1 (.Clock(clock_1_out), .tv(controller_1_tv), .zv(timerv_1_zv));
  TimerA timera_1 (.Clock(clock_1_out), .ta(controller_1_ta), .za(timera_1_za));
endmodule

module Controller (
  input  sa,
  input  za,
  input  sv,
  input  zv,
  input  Clock,
  output pa,
  output ta,
  output pv,
  output tv
);

  wire and_1_out, and_2_out, and_3_out, and_4_out, and_5_out, and_6_out, and_11_out, and_12_out, d_ff_1_q,
       d_ff_2_q, d_ff_3_q, not_2_out, not_3_out, not_4_out, not_6_out, not_7_out, or_1_out, or_2_out,
       or_3_out, or_4_out, or_5_out;

  // NOT_Gate not_1 has open pins: in=sa, out=open
  not not_2 (not_2_out, za);
  not not_3 (not_3_out, sv);
  not not_4 (not_4_out, d_ff_1_q);
  // NOT_Gate not_5 has open pins: in=zv, out=open
  D_Flip_Flop d_ff_1 (.clk(Clock), .D(or_3_out), .Q(d_ff_1_q));  // open: Qn, preset, en, reset
  not not_6 (not_6_out, d_ff_3_q);
  not not_7 (not_7_out, d_ff_2_q);
  D_Flip_Flop d_ff_2 (.clk(Clock), .D(or_4_out), .Q(d_ff_2_q));  // open: Qn, preset, en, reset
  and and_1 (and_1_out, not_4_out, d_ff_2_q, d_ff_3_q);
  and and_2 (and_2_out, d_ff_1_q, not_7_out, not_6_out, not_3_out);
  or or_1 (or_1_out, sa, za);
  and and_3 (and_3_out, not_4_out, d_ff_2_q, not_6_out);
  and and_4 (and_4_out, not_4_out, not_7_out, not_6_out);
  or or_2 (or_2_out, sa, not_2_out);
  and and_5 (and_5_out, not_4_out, d_ff_2_q, not_6_out);
  and and_6 (and_6_out, d_ff_1_q, not_7_out, not_6_out, not_3_out, zv);
  and and_7 (pa, not_4_out, d_ff_2_q, not_6_out);
  and and_8 (ta, not_4_out, not_7_out, not_6_out);
  and and_9 (pv, d_ff_1_q, not_7_out, d_ff_3_q);
  and and_10 (tv, not_4_out, d_ff_2_q, d_ff_3_q);
  D_Flip_Flop d_ff_3 (.clk(Clock), .D(or_5_out), .Q(d_ff_3_q));  // open: Qn, preset, en, reset
  or or_3 (or_3_out, and_1_out, and_2_out);
  and and_11 (and_11_out, or_1_out, not_4_out, not_7_out, d_ff_3_q);
  and and_12 (and_12_out, or_2_out, not_4_out, not_7_out, d_ff_3_q);
  or or_4 (or_4_out, and_11_out, and_3_out);
  or or_5 (or_5_out, and_4_out, and_12_out, and_5_out, and_6_out);
endmodule

module TimerA (
  input  Clock,
  input  ta,
  output za
);

  wire d_ff_1_q, d_ff_2_q, d_ff_3_q, d_ff_4_q, d_ff_5_q, d_ff_6_q, incrementer_1_s0, incrementer_1_s1,
       incrementer_1_s2, incrementer_1_s3, incrementer_1_s4, incrementer_1_s5;

  D_Flip_Flop d_ff_1 (.clk(Clock), .D(incrementer_1_s5), .Q(d_ff_1_q), .reset(ta));  // open: Qn, preset, en
  D_Flip_Flop d_ff_2 (.clk(Clock), .D(incrementer_1_s4), .Q(d_ff_2_q), .reset(ta));  // open: Qn, preset, en
  D_Flip_Flop d_ff_3 (.clk(Clock), .D(incrementer_1_s3), .Q(d_ff_3_q), .reset(ta));  // open: Qn, preset, en
  D_Flip_Flop d_ff_4 (.clk(Clock), .D(incrementer_1_s2), .Q(d_ff_4_q), .reset(ta));  // open: Qn, preset, en
  D_Flip_Flop d_ff_5 (.clk(Clock), .D(incrementer_1_s1), .Q(d_ff_5_q), .reset(ta));  // open: Qn, preset, en
  D_Flip_Flop d_ff_6 (.clk(Clock), .D(incrementer_1_s0), .Q(d_ff_6_q), .reset(ta));  // open: Qn, preset, en
  Incrementer incrementer_1 (
    .a3(d_ff_3_q), .a2(d_ff_4_q), .a1(d_ff_5_q), .a0(d_ff_6_q), .s3(incrementer_1_s3), .s2(incrementer_1_s2),
    .s1(incrementer_1_s1), .s0(incrementer_1_s0), .a4(d_ff_2_q), .s4(incrementer_1_s4), .a5(d_ff_1_q),
    .s5(incrementer_1_s5));  // open: co
  Comparator comparator_1 (
    .in_1(d_ff_1_q), .in_2(1'b1), .in_3(d_ff_2_q), .in_4(1'b0), .in_5(d_ff_3_q), .in_6(1'b1),
    .in_7(d_ff_4_q), .in_8(1'b1), .in_9(d_ff_5_q), .in_10(1'b0), .out_13(za), .in_11(d_ff_6_q), .in_12(1'b1));
endmodule

module TimerV (
  input  Clock,
  input  tv,
  output zv
);

  wire d_ff_1_q, d_ff_2_q, d_ff_3_q, d_ff_4_q, d_ff_5_q, d_ff_6_q, incrementer_1_s0, incrementer_1_s1,
       incrementer_1_s2, incrementer_1_s3, incrementer_1_s4, incrementer_1_s5;

  D_Flip_Flop d_ff_1 (.clk(Clock), .D(incrementer_1_s5), .Q(d_ff_1_q), .reset(tv));  // open: Qn, preset, en
  D_Flip_Flop d_ff_2 (.clk(Clock), .D(incrementer_1_s4), .Q(d_ff_2_q), .reset(tv));  // open: Qn, preset, en
  D_Flip_Flop d_ff_3 (.clk(Clock), .D(incrementer_1_s3), .Q(d_ff_3_q), .reset(tv));  // open: Qn, preset, en
  D_Flip_Flop d_ff_4 (.clk(Clock), .D(incrementer_1_s2), .Q(d_ff_4_q), .reset(tv));  // open: Qn, preset, en
  D_Flip_Flop d_ff_5 (.clk(Clock), .D(incrementer_1_s1), .Q(d_ff_5_q), .reset(tv));  // open: Qn, preset, en
  D_Flip_Flop d_ff_6 (.clk(Clock), .D(incrementer_1_s0), .Q(d_ff_6_q), .reset(tv));  // open: Qn, preset, en
  Incrementer incrementer_1 (
    .a3(d_ff_3_q), .a2(d_ff_4_q), .a1(d_ff_5_q), .a0(d_ff_6_q), .s3(incrementer_1_s3), .s2(incrementer_1_s2),
    .s1(incrementer_1_s1), .s0(incrementer_1_s0), .a4(d_ff_2_q), .s4(incrementer_1_s4), .a5(d_ff_1_q),
    .s5(incrementer_1_s5));  // open: co
  Comparator comparator_1 (
    .in_1(d_ff_1_q), .in_2(1'b0), .in_3(d_ff_2_q), .in_4(1'b1), .in_5(d_ff_3_q), .in_6(1'b1),
    .in_7(d_ff_4_q), .in_8(1'b1), .in_9(d_ff_5_q), .in_10(1'b1), .out_13(zv), .in_11(d_ff_6_q), .in_12(1'b0));
endmodule

module Incrementer (
  input  a5,
  input  a4,
  input  a3,
  input  a2,
  input  a1,
  input  a0,
  output co,
  output s5,
  output s4,
  output s3,
  output s2,
  output s1,
  output s0
);

  wire half_adder_2_cj, half_adder_3_cj, half_adder_4_cj, half_adder_5_cj, half_adder_6_cj;

  Half_Adder half_adder_1 (.Xi(a5), .Yi(half_adder_2_cj), .Cj(co), .S(s5));
  Half_Adder half_adder_2 (.Xi(a4), .Yi(half_adder_3_cj), .Cj(half_adder_2_cj), .S(s4));
  Half_Adder half_adder_3 (.Xi(a3), .Yi(half_adder_4_cj), .Cj(half_adder_3_cj), .S(s3));
  Half_Adder half_adder_4 (.Xi(a2), .Yi(half_adder_5_cj), .Cj(half_adder_4_cj), .S(s2));
  Half_Adder half_adder_5 (.Xi(a1), .Yi(half_adder_6_cj), .Cj(half_adder_5_cj), .S(s1));
  Half_Adder half_adder_6 (.Xi(a0), .Yi(1'b1), .Cj(half_adder_6_cj), .S(s0));
endmodule

module Half_Adder (
  input  Xi,
  input  Yi,
  output Cj,
  output S
);

  and and_1 (Cj, Xi, Yi);
  xor xor_1 (S, Xi, Yi);
endmodule

module Comparator (
  input  in_1,
  input  in_2,
  input  in_3,
  input  in_4,
  input  in_5,
  input  in_6,
  input  in_7,
  input  in_8,
  input  in_9,
  input  in_10,
  input  in_11,
  input  in_12,
  output out_13
);

  wire xnor_1_out, xnor_2_out, xnor_3_out, xnor_4_out, xnor_5_out, xnor_6_out;

  xnor xnor_1 (xnor_1_out, in_1, in_2);
  xnor xnor_2 (xnor_2_out, in_3, in_4);
  xnor xnor_3 (xnor_3_out, in_5, in_6);
  xnor xnor_4 (xnor_4_out, in_7, in_8);
  and and_1 (out_13, xnor_1_out, xnor_2_out, xnor_3_out, xnor_4_out, xnor_5_out, xnor_6_out);
  xnor xnor_5 (xnor_5_out, in_9, in_10);
  xnor xnor_6 (xnor_6_out, in_11, in_12);
endmodule
